# Fritzing sketch lab2sketch (saved by Fritzing 0.9.4)
breadboards: 3

parts:
  U2 = 74109 Dual Positive Edge J K Flip Flop [part_number=74109 package="DIP16 [THT]"]
  U3 = 7400 4 x 2 Input NAND Gate [part_number=7400 package="DIP (Dual Inline) [THT]"]
  U4 = 7400 4 x 2 Input NAND Gate [part_number=7400 package="DIP (Dual Inline) [THT]"]
  U5 = 7402 4 x 2 Input NOR Gate [part_number=7402 package="DIP (Dual Inline) [THT]"]
  U6 = 7486 4 x 2 Input XOR Gate [part_number=7486 package="DIP (Dual Inline) [THT]"]
  U7 = 74153 Dual 4:1 MUX [part_number=74153 package="DIP16 [THT]"]
  U9 = 74194 4 Bit Bi-Directional Shift Register [part_number=74194 package="DIP16 [THT]"]
  U10 = 74194 4 Bit Bi-Directional Shift Register [part_number=74194 package="DIP16 [THT]"]
  U11 = 7402 4 x 2 Input NOR Gate [part_number=7402 package="DIP (Dual Inline) [THT]"]
  U12 = 74153 Dual 4:1 MUX [part_number=74153 package="DIP16 [THT]"]
  U13 = 74161 4 Bit Synchronous Up Down Counter [part_number=74161 package="DIP16 [THT]"]

nets:
  GND: U2.GND, U3.GND, U4.GND, U5.GND, U6.GND, U7.G1, U7.G0, U7.GND, U7.S1, U9.GND, U10.GND, U11.GND, U12.G0, U12.GND, U13.7, U13.GND
  N1: U2.MR, U4.A4, U4.B4
  VCC: U2.SH_CP, U2.Q0, U2.VCC, U3.VDD, U4.VDD, U5.VDD, U6.VDD, U7.VCC, U9.1, U9.VCC, U10.1, U10.VCC, U11.VDD, U12.D0, U12.VCC, U13.9, U13.10, U13.VCC
  N2: U2.OE, U2.DS, U3.B2
  N3: U3.A1, U3.B1, U3.B4
  N4: U3.Q1, U3.Q2
  N5: U3.A2, U3.B3
  N6: U3.A3, U5.B4, U11.B3, U11.Q4, U13.1
  N7: U3.Q3, U3.Q4
  N8: U3.A4, U4.Q4
  N9: U4.A1, U5.B1, U6.A1, U7.D0, U7.C1, U7.A1, U10.12
  N10: U4.B1, U5.Q1, U6.B1, U7.A0, U7.B0, U7.D1, U9.12
  N11: U4.Q1, U4.Q2, U4.A2
  N12: U4.B2, U12.A0
  N13: U5.A1, U5.A2, U5.B2
  N14: U5.Q2, U12.B0
  N15: U5.Q4, U13.14
  N16: U5.A4, U13.13
  N17: U6.Q1, U12.C0
  N18: U6.A2, U12.Y0
  N19: U6.B2, U7.C0, U7.B1
  N20: U7.Y1, U10.2
  N21: U7.Y0, U9.2
  N22: U9.9, U11.A1
  N23: U9.10, U11.A4
  N24: U9.11, U10.11
  N25: U10.9, U11.Q2
  N26: U10.10, U11.A3
  N27: U11.B1, U11.Q1, U11.B4
  N28: U11.A2, U11.B2, U11.Q3

notes:
  Q
  Execute
  CLK
  loadA
  Din
  loadB
  [F0]
  F1
  R1
  R0
  F2
  output RegA
  output RegB
  control unit

custom parts:
  74153 Dual 4:1 MUX: 74153 Dual 4:1 Multiplexor
